// Logisim project riscv.circ as structural Verilog: 6 circuits, main circuit MAIN
module MAIN (
);

  wire ADD, ADI, ALU_ENABLE, AND, ANI, CLK, COUNTER_CLEAR, HLT, IR_ENABLE, LOAD, MEM_CLEAR, MEM_READ,
       MEM_WRITE, MOV, MUX_STORE_SELECT, MUXB_ENABLE, MUXB_SELECT, MUXMEM_SELECT, MUXY_ENABLE, MUXY_SELECT,
       MVI, OR, ORI, PC_ENABLE, PC_STOP, RA_ENABLE, RA_ENABLE_SELECT, RB_ENABLE, RB_ENABLE_SELECT, RM_ENABLE,
       RY_ENABLE, RY_ENABLE_SELECT, RZ_ENABLE, STAGE_1, STAGE_2, STAGE_3, STAGE_4, STAGE_5, STORE, SUB, SUI;
  wire [3:0] ALU_SELECT, OPCODE, RA_SELECT, RB_SELECT, RY_SELECT;
  wire [15:0] bit_extender_1_out, MEM_ADDR, PC_OUTPUT;
  wire [31:0] alu_1_output, IM_VALUE, MEM_OUTPUT, multiplexer_1_out, multiplexer_2_out, RA_q, RB_q,
       rf_1_ra_out, rf_1_rb_out, RM_OUTPUT, RY_q, RZ_q;

  CU cu_1 (
    .CLK(CLK), .MOV(MOV), .RA_ENABLE(RA_ENABLE), .ALU_ENABLE(ALU_ENABLE), .OPCODE(OPCODE), .MVI(MVI),
    .RB_ENABLE(RB_ENABLE), .ALU_SELECT(ALU_SELECT), .COUNTER_CLEAR(COUNTER_CLEAR), .LOAD(LOAD),
    .RM_ENABLE(RM_ENABLE), .MUXB_ENABLE(MUXB_ENABLE), .STORE(STORE), .RZ_ENABLE(RZ_ENABLE),
    .MUXB_SELECT(MUXB_SELECT), .STAGE_1(STAGE_1), .ADD(ADD), .RY_ENABLE(RY_ENABLE),
    .MUXY_ENABLE(MUXY_ENABLE), .STAGE_2(STAGE_2), .STAGE_3(STAGE_3), .ADI(ADI),
    .RA_ENABLE_SELECT(RA_ENABLE_SELECT), .MUXY_SELECT(MUXY_SELECT), .STAGE_4(STAGE_4), .SUB(SUB),
    .RB_ENABLE_SELECT(RB_ENABLE_SELECT), .MUXMEM_SELECT(MUXMEM_SELECT), .STAGE_5(STAGE_5), .SUI(SUI),
    .RY_ENABLE_SELECT(RY_ENABLE_SELECT), .PC_ENABLE(PC_ENABLE), .AND(AND), .IR_ENABLE(IR_ENABLE),
    .MEM_READ(MEM_READ), .ANI(ANI), .MEM_WRITE(MEM_WRITE), .PC_STOP(PC_STOP), .OR(OR),
    .MUX_STORE_SELECT(MUX_STORE_SELECT), .ORI(ORI), .HLT(HLT));
  RAM #(.addrWidth(16), .dataWidth(32), .bus("separate")) ram_1 (
    .addr(MEM_ADDR), .din(RM_OUTPUT), .data(MEM_OUTPUT), .str(MEM_WRITE), .sel(1'b1), .clk(CLK),
    .ld(MEM_READ), .clr(MEM_CLEAR));
  Button button_1 (.out(COUNTER_CLEAR));
  Button button_2 (.out(MEM_CLEAR));
  Clock clock_1 (.out(CLK));
  // Probe on rf_1_ra_out
  // Probe on rf_1_rb_out
  // Probe on PC_OUTPUT
  // Probe on MEM_OUTPUT
  // Probe on IM_VALUE
  // Probe on RB_SELECT
  // Probe on RA_q
  // Probe on multiplexer_1_out
  // Probe on alu_1_output
  // Probe on multiplexer_2_out
  // Probe on RY_q
  // Probe on RA_SELECT
  // Probe on RY_SELECT
  // Probe on MEM_ADDR
  LED led_1 (.in(STAGE_1));
  LED led_2 (.in(STAGE_2));
  LED led_3 (.in(STAGE_3));
  LED led_4 (.in(STAGE_4));
  LED led_5 (.in(STAGE_5));
  RF rf_1 (
    .DATA_IN(RY_q), .CLOCK(CLK), .CLEAR(COUNTER_CLEAR), .RA_OUT(rf_1_ra_out), .SELECT_RA(RA_SELECT),
    .SELECT_RB(RB_SELECT), .SELECT_RO(RY_SELECT), .RB_OUT(rf_1_rb_out), .RO_ENABLE_SELECT(RY_ENABLE_SELECT),
    .RA_ENABLE_SELECT(RA_ENABLE_SELECT), .RB_ENABLE_SELECT(RB_ENABLE_SELECT), .RO_RB_BYPASS(MUX_STORE_SELECT));
  Register #(.width(32)) RA (.D(rf_1_ra_out), .en(RA_ENABLE), .Q(RA_q), .clk(CLK), .clr(COUNTER_CLEAR));
  LED led_6 (.in(ADD));
  LED led_7 (.in(SUB));
  LED led_8 (.in(AND));
  LED led_9 (.in(OR));
  ALU alu_1 (
    .ALU_SELECT(ALU_SELECT), .INPUT_A(RA_q), .OUTPUT(alu_1_output), .INPUT_B(multiplexer_1_out),
    .ALU_ENABLE(ALU_ENABLE));
  Register #(.width(32)) RZ (.D(alu_1_output), .en(RZ_ENABLE), .Q(RZ_q), .clk(CLK), .clr(COUNTER_CLEAR));
  LED led_10 (.in(ADI));
  LED led_11 (.in(SUI));
  LED led_12 (.in(ADI));
  LED led_13 (.in(ORI));
  Register #(.width(32)) RB (.D(rf_1_rb_out), .en(RB_ENABLE), .Q(RB_q), .clk(CLK), .clr(COUNTER_CLEAR));
  Multiplexer #(.width(32)) multiplexer_1 (
    .in0(RB_q), .in1(IM_VALUE), .out(multiplexer_1_out), .sel(MUXB_SELECT), .en(MUXB_ENABLE));
  // Probe on RZ_q
  LED led_14 (.in(MOV));
  LED led_15 (.in(HLT));
  LED led_16 (.in(MVI));
  LED led_17 (.in(LOAD));
  LED led_18 (.in(STORE));
  Multiplexer #(.width(32)) multiplexer_2 (
    .in0(RZ_q), .in1(MEM_OUTPUT), .out(multiplexer_2_out), .sel(MUXY_SELECT), .en(MUXY_ENABLE));
  Bit_Extender #(.in_width(32)) bit_extender_1 (.in(RZ_q), .out(bit_extender_1_out));
  Register #(.width(32)) RY (.D(multiplexer_2_out), .en(RY_ENABLE), .Q(RY_q), .clk(CLK), .clr(COUNTER_CLEAR));
  Register #(.width(32)) RM (.D(RB_q), .en(RM_ENABLE), .Q(RM_OUTPUT), .clk(CLK), .clr(COUNTER_CLEAR));
  Multiplexer #(.width(16), .enable("false")) multiplexer_3 (
    .in0(PC_OUTPUT), .in1(bit_extender_1_out), .out(MEM_ADDR), .sel(MUXMEM_SELECT));
  DECODER decoder_1 (
    .INPUT(MEM_OUTPUT), .IMMEDIATE(IM_VALUE), .CLOCK(CLK), .RA_SELECT(RA_SELECT), .OPCODE(OPCODE),
    .RB_SELECT(RB_SELECT), .RY_SELECT(RY_SELECT), .IR_ENABLE(IR_ENABLE), .IR_CLEAR(COUNTER_CLEAR));
  Decoder #(.select(4), .enable("false")) decoder_2 (
    .out0(ADD), .out1(ADI), .out2(SUB), .out3(SUI), .out4(AND), .out5(ANI), .out6(OR), .out7(ORI),
    .out8(MOV), .out9(MVI), .out10(LOAD), .out11(STORE), .out15(HLT), .sel(OPCODE));  // open: out12, out13, out14
  IAG iag_1 (.CLOCK(CLK), .PC_ENABLE(PC_ENABLE), .PC(PC_OUTPUT), .CLEAR(COUNTER_CLEAR));

  // Other names for the same wires on the sheet: IR_CLEAR = COUNTER_CLEAR; PC__CLEAR = COUNTER_CLEAR;
  //   RA_CLEAR = COUNTER_CLEAR; RB_CLEAR = COUNTER_CLEAR; RF_CLEAR = COUNTER_CLEAR; RM_CLEAR = COUNTER_CLEAR;
  //   RY_CLEAR = COUNTER_CLEAR; RZ_CLEAR = COUNTER_CLEAR

  // Notes on the sheet:
  //   KAUSHIK DEY
  //   20CS01043 - SEMESTER 5
  //   COA LAB - MINI PROJECT
  //   CONTROL SIGNALS
  //   MEMORY INTERFACE
  //   RESET
  //   MAIN CIRCUIT
  //   PROBES
  //   DATAPATH
  //   INSTRUCTION DECODER
endmodule

module CU (
  input  CLK,
  input  MOV,
  input  [3:0] OPCODE,
  input  MVI,
  input  COUNTER_CLEAR,
  input  LOAD,
  input  STORE,
  input  ADD,
  input  ADI,
  input  SUB,
  input  SUI,
  input  AND,
  input  ANI,
  input  OR,
  input  ORI,
  input  HLT,
  output RA_ENABLE,
  output ALU_ENABLE,
  output RB_ENABLE,
  output [3:0] ALU_SELECT,
  output RM_ENABLE,
  output MUXB_ENABLE,
  output RZ_ENABLE,
  output MUXB_SELECT,
  output STAGE_1,
  output RY_ENABLE,
  output MUXY_ENABLE,
  output STAGE_2,
  output STAGE_3,
  output RA_ENABLE_SELECT,
  output MUXY_SELECT,
  output STAGE_4,
  output RB_ENABLE_SELECT,
  output MUXMEM_SELECT,
  output STAGE_5,
  output RY_ENABLE_SELECT,
  output PC_ENABLE,
  output IR_ENABLE,
  output MEM_READ,
  output MEM_WRITE,
  output PC_STOP,
  output MUX_STORE_SELECT
);

  wire and_11_out, or_5_out, or_7_out, TYPE_1, TYPE_2, TYPE_3, TYPE_4;
  wire [2:0] counter_1_q;

  Decoder #(.select(3), .enable("false")) decoder_1 (
    .out0(STAGE_1), .out1(STAGE_2), .out2(STAGE_3), .out3(STAGE_4), .out4(STAGE_5), .sel(counter_1_q));  // open: out5, out6, out7
  Counter #(.width(3), .max('h4)) counter_1 (
    .D(3'b000), .Q(counter_1_q), .clk(CLK), .clr(COUNTER_CLEAR));  // open: load, count, carry
  or or_1 (TYPE_1, ADD, ADI, SUB, SUI, AND, ANI, OR, ORI, MOV, MVI, LOAD, STORE);
  or or_2 (TYPE_2, LOAD, MVI, ADI, SUI, ANI, ORI);
  or or_3 (TYPE_3, ADD, SUB, AND, OR, STORE);
  or or_4 (TYPE_4, ADD, ADI, SUB, SUI, AND, ANI, HLT, OR, ORI, MOV, MVI, LOAD, STORE);
  and and_1 (IR_ENABLE, STAGE_1, TYPE_1);
  and and_2 (MUXY_ENABLE, STAGE_4, TYPE_1);
  and and_3 (MUXMEM_SELECT, STAGE_4, or_5_out);
  or or_5 (or_5_out, STORE, LOAD);
  and and_4 (MUXY_SELECT, STAGE_4, LOAD);
  and and_5 (MEM_WRITE, STAGE_4, STORE);
  and and_6 (MEM_READ, STAGE_4, LOAD);
  and and_7 (MEM_READ, STAGE_1, TYPE_4);
  and and_8 (MUX_STORE_SELECT, STAGE_2, STORE);
  and and_9 (PC_STOP, STAGE_2, HLT);
  and and_10 (RB_ENABLE, STAGE_2, TYPE_3);
  and and_11 (and_11_out, STAGE_2, TYPE_2);
  or or_6 (RA_ENABLE, RB_ENABLE, MOV, and_11_out);
  and and_12 (RY_ENABLE_SELECT, STAGE_5, TYPE_1);
  or or_7 (or_7_out, STORE, TYPE_2);
  and and_13 (ALU_ENABLE, STAGE_3, TYPE_1);
  and and_14 (MUXB_SELECT, STAGE_3, or_7_out);
  and and_15 (RM_ENABLE, STAGE_3, STORE);

  assign ALU_SELECT = OPCODE;
  assign MUXB_ENABLE = ALU_ENABLE;
  assign PC_ENABLE = IR_ENABLE;
  assign RA_ENABLE_SELECT = RA_ENABLE;
  assign RB_ENABLE_SELECT = RB_ENABLE;
  assign RY_ENABLE = MUXY_ENABLE;
  assign RZ_ENABLE = ALU_ENABLE;

  // Other names for the same wires on the sheet: Stage1 = STAGE_1; Stage2 = STAGE_2; Stage3 = STAGE_3;
  //   Stage4 = STAGE_4; Stage5 = STAGE_5

  // Notes on the sheet:
  //   OPCODES
  //   STAGE COUNTER
  //   CONTROL UNIT
  //   SIGNALS
  //   STAGE 1
  //   STAGE 4
  //   INSTRUCTION FETCHING
  //   STAGE 2
  //   STAGE 5
  //   MISC
  //   STAGE 3
endmodule

module ALU (
  input  [3:0] ALU_SELECT,
  input  ALU_ENABLE,
  input  [31:0] INPUT_A,
  input  [31:0] INPUT_B,
  output [31:0] OUTPUT
);

  wire [31:0] AND, DIFF, OR, SUM;

  Adder #(.width(32)) adder_1 (.a(INPUT_A), .b(INPUT_B), .out(SUM), .cin(1'b0));  // open: cout
  assign OR = INPUT_A | INPUT_B;  // OR_Gate or_1, 32 bits wide
  Subtractor #(.width(32)) subtractor_1 (.a(INPUT_A), .b(INPUT_B), .out(DIFF), .bin(1'b0));  // open: bout
  assign AND = INPUT_A & INPUT_B;  // AND_Gate and_1, 32 bits wide
  Multiplexer #(.select(4), .width(32)) multiplexer_1 (
    .in0(SUM), .in1(SUM), .in2(DIFF), .in3(DIFF), .in4(AND), .in5(AND), .in6(OR), .in7(OR), .in8(INPUT_A),
    .in9(INPUT_B), .in10(SUM), .in11(SUM), .out(OUTPUT), .sel(ALU_SELECT), .en(ALU_ENABLE));  // open: in12, in13, in14, in15

  // Other names for the same wires on the sheet: ENABLE = ALU_ENABLE; IN_A[31:0] = INPUT_A; IN_B[31:0] = INPUT_B;
  //   OPCODE[3:0] = ALU_SELECT; RES[31:0] = OUTPUT

  // Notes on the sheet:
  //   ARITHMETIC OPERATIONS
  //   LOGICAL OPERATIONS
  //   ARITHMETIC AND LOGIC UNIT
  //   OPERATION DECODER
endmodule

module RF (
  input  [31:0] DATA_IN,
  input  RO_ENABLE_SELECT,
  input  CLOCK,
  input  RA_ENABLE_SELECT,
  input  RB_ENABLE_SELECT,
  input  CLEAR,
  input  RO_RB_BYPASS,
  input  [3:0] SELECT_RA,
  input  [3:0] SELECT_RB,
  input  [3:0] SELECT_RO,
  output [31:0] RA_OUT,
  output [31:0] RB_OUT
);

  wire EN_R1, EN_R2, EN_R3, EN_R4, EN_R5, EN_R6, EN_R7, EN_R8;
  wire [3:0] multiplexer_3_out;
  wire [31:0] R1_OUT, R2_OUT, R3_OUT, R4_OUT, R5_OUT, R6_OUT, R7_OUT, R8_OUT;

  Register #(.width(32)) register_1 (.D(DATA_IN), .en(EN_R1), .Q(R1_OUT), .clk(CLOCK), .clr(CLEAR));
  Register #(.width(32)) register_2 (.D(DATA_IN), .en(EN_R3), .Q(R3_OUT), .clk(CLOCK), .clr(CLEAR));
  Register #(.width(32)) register_3 (.D(DATA_IN), .en(EN_R5), .Q(R5_OUT), .clk(CLOCK), .clr(CLEAR));
  // Probe on R1_OUT
  // Probe on R2_OUT
  // Probe on R3_OUT
  // Probe on R4_OUT
  // Probe on R5_OUT
  // Probe on R6_OUT
  // Probe on R7_OUT
  // Probe on R8_OUT
  Register #(.width(32)) register_4 (.D(DATA_IN), .en(EN_R2), .Q(R2_OUT), .clk(CLOCK), .clr(CLEAR));
  Register #(.width(32)) register_5 (.D(DATA_IN), .en(EN_R4), .Q(R4_OUT), .clk(CLOCK), .clr(CLEAR));
  Register #(.width(32)) register_6 (.D(DATA_IN), .en(EN_R6), .Q(R6_OUT), .clk(CLOCK), .clr(CLEAR));
  Register #(.width(32)) register_7 (.D(DATA_IN), .en(EN_R7), .Q(R7_OUT), .clk(CLOCK), .clr(CLEAR));
  Register #(.width(32)) register_8 (.D(DATA_IN), .en(EN_R8), .Q(R8_OUT), .clk(CLOCK), .clr(CLEAR));
  Multiplexer #(.select(4), .width(32)) multiplexer_1 (
    .in0(R1_OUT), .in1(R2_OUT), .in2(R3_OUT), .in3(R4_OUT), .in4(R5_OUT), .in5(R6_OUT), .in6(R7_OUT),
    .in7(R8_OUT), .out(RA_OUT), .sel(SELECT_RA), .en(RA_ENABLE_SELECT));  // open: in8, in9, in10, in11, in12, in13, in14, in15
  Demultiplexer #(.select(4), .enable("false")) demultiplexer_1 (
    .out0(EN_R1), .out1(EN_R2), .out2(EN_R3), .out3(EN_R4), .out4(EN_R5), .out5(EN_R6), .out6(EN_R7),
    .out7(EN_R8), .in(RO_ENABLE_SELECT), .sel(SELECT_RO));  // open: out8, out9, out10, out11, out12, out13, out14, out15
  Multiplexer #(.select(4), .width(32)) multiplexer_2 (
    .in0(R1_OUT), .in1(R2_OUT), .in2(R3_OUT), .in3(R4_OUT), .in4(R5_OUT), .in5(R6_OUT), .in6(R7_OUT),
    .in7(R8_OUT), .out(RB_OUT), .sel(multiplexer_3_out), .en(RB_ENABLE_SELECT));  // open: in8, in9, in10, in11, in12, in13, in14, in15
  Multiplexer #(.width(4), .enable("false")) multiplexer_3 (
    .in0(SELECT_RB), .in1(SELECT_RO), .out(multiplexer_3_out), .sel(RO_RB_BYPASS));

  // Other names for the same wires on the sheet: CLK = CLOCK; CLR = CLEAR; ENABLE_RA_SELECT = RA_ENABLE_SELECT;
  //   ENABLE_RB_SELECT = RB_ENABLE_SELECT; ENABLE_RO_SELECT = RO_ENABLE_SELECT; RA[31:0] = RA_OUT; RB[31:0] = RB_OUT;
  //   RIN[31:0] = DATA_IN; SEL_RA[3:0] = SELECT_RA; SEL_RB[3:0] = SELECT_RB; SEL_RO[3:0] = SELECT_RO

  // Notes on the sheet:
  //   REGISTER FILE
  //   REGISTER PROBES
  //   RA SELECT
  //   WRITE SELECT
  //   RB SELECT
endmodule

module IAG (
  input  CLOCK,
  input  PC_ENABLE,
  input  CLEAR,
  output [15:0] PC
);

  wire [15:0] adder_1_out;

  Register #(.width(16)) u_PC (.D(adder_1_out), .en(PC_ENABLE), .Q(PC), .clk(CLOCK), .clr(CLEAR));
  Adder #(.width(16)) adder_1 (.a(PC), .b(16'h1), .out(adder_1_out));  // open: cin, cout

  // Other names for the same wires on the sheet: CLK = CLOCK

  // Notes on the sheet:
  //   INSTRUCTION ADDRESS GENERATOR
endmodule

module DECODER (
  input  [31:0] INPUT,
  input  CLOCK,
  input  IR_ENABLE,
  input  IR_CLEAR,
  output [31:0] IMMEDIATE,
  output [3:0] RA_SELECT,
  output [3:0] OPCODE,
  output [3:0] RB_SELECT,
  output [3:0] RY_SELECT
);

  Register #(.width(32)) IR (
    .D(INPUT), .en(IR_ENABLE), .Q({OPCODE, RY_SELECT, RA_SELECT, RB_SELECT, IMMEDIATE[15:0]}), .clk(CLOCK),
    .clr(IR_CLEAR));

  assign IMMEDIATE[31:16] = {16{1'b0}};

  // Other names for the same wires on the sheet: CLK = CLOCK; IM[15:0] = IMMEDIATE[15:0];
  //   TEMP[15:0] = IMMEDIATE[15:0]; INST[31:0] = INPUT

  // Notes on the sheet:
  //   INSTRUCTION DECODER
endmodule
